# Fritzing sketch arduino (saved by Fritzing 0.9.3b)
breadboards: 1

parts:
  Componente1 = Arduino Uno (Rev3)
  RHT1 = Humidity and Temperature Sensor RHT03
  Componente2 = Soil Moisture Sensor
  R2 = Resistor [tolerance=±5% resistance=220 package=THT]
  Componente3 = Arduino Uno (Rev3)  # not connected
  Componente4 = Bluetooth HC-05 Macho  # not connected
  Componente5 = Soil Moisture Sensor

nets:
  N1: Componente1.A1, Componente2.SIG
  N2: Componente1.A2, Componente5.SIG
  VCC: Componente1.5V, Componente2.VCC, R2.Pin_0, R2.Pin_1, Componente5.VCC
  GND: Componente1.GND, RHT1.GND_1, Componente2.GND, Componente5.GND
